// Logisim project ALU_.circ as structural Verilog: 1 circuit, main circuit main
module main (
  input  F1_1,
  input  F1_4,
  input  F2_1,
  input  F2_2,
  input  F2_3,
  input  F3_1,
  input  F3_2,
  input  F3_3,
  input  F3_4,
  output LD_AC
);

  or or_1 (LD_AC, F1_1, F1_4, F2_1, F2_2, F2_3, F3_1, F3_2, F3_3, F3_4);
endmodule
