// Logisim project AR.circ as structural Verilog: 1 circuit, main circuit main
module main (
  input  [10:0] d,
  input  LD,
  input  inr,
  input  clk,
  input  clr,
  output [10:0] Q
);

  wire main_1_p2, main_2_p1, main_2_p4, main_3_p2, main_4_p2, main_5_p1, main_6_p1, main_7_p2, main_8_p1,
       main_9_p2, main_10_p1, main_11_p3, or_1_out;
  wire [10:0] main_11_p1, multiplexer_1_out;

  Multiplexer #(.width(11), .enable("false")) multiplexer_1 (
    .in0(d), .in1(main_11_p1), .out(multiplexer_1_out), .sel(inr));
  // half_adder_main main_1: pin names not known; wires that end beside it: main_11_p1[9], main_1_p2, Q[9], main_1_p2
  // half_adder_main main_2: pin names not known; wires that end beside it: main_2_p1, main_11_p1[10], main_2_p1, main_2_p4, Q[10], main_2_p4
  // half_adder_main main_3: pin names not known; wires that end beside it: main_11_p1[8], main_3_p2, Q[8], main_11_p1[7], main_3_p2
  // half_adder_main main_4: pin names not known; wires that end beside it: main_11_p1[6], main_4_p2, Q[6], main_11_p1[5], main_4_p2
  // half_adder_main main_5: pin names not known; wires that end beside it: main_5_p1, Q[7], main_5_p1
  // half_adder_main main_6: pin names not known; wires that end beside it: main_6_p1, Q[5], main_11_p1[4], main_6_p1
  or or_1 (or_1_out, LD, inr);
  // half_adder_main main_7: pin names not known; wires that end beside it: main_11_p1[3], main_7_p2, Q[3], main_11_p1[2], main_7_p2
  // half_adder_main main_8: pin names not known; wires that end beside it: main_8_p1, Q[4], main_8_p1
  // half_adder_main main_9: pin names not known; wires that end beside it: main_11_p1[1], main_9_p2, Q[1], main_9_p2
  // half_adder_main main_10: pin names not known; wires that end beside it: main_10_p1, Q[2], main_10_p1
  // half_adder_main main_11: pin names not known; wires that end beside it: main_11_p1[0], 1'b1, main_11_p3
  and and_1 (main_11_p3, inr, Q[0]);
  Register #(.width(11)) register_1 (.D(multiplexer_1_out), .en(or_1_out), .Q(Q), .clk(clk), .clr(clr));
endmodule
