// Logisim project COMPUTER2_0.circ as structural Verilog: 1 circuit, main circuit main
module main (
  input  CLK,
  input  in_2,
  input  [6:0] init_add,
  input  S,
  output [6:0] sbr,
  output [1:0] s0s1,
  output [6:0] mux_op,
  output [10:0] pc,
  output [10:0] AR,
  output [6:0] ad_cm,
  output [15:0] DR,
  output [15:0] AC
);

  wire j_k_ff_1_q, main_1_p30, main_3_p1, main_3_p4, not_1_out, not_2_out, not_3_out, not_4_out, or_1_out,
       or_2_out, or_3_out, or_4_out, or_5_out;
  wire [6:0] CAR_q, main_2_q, rom_1_data;
  wire [7:0] decoder_1_out7, decoder_2_out6, decoder_3_out7;
  wire [10:0] multiplexer_1_out;
  wire [15:0] bit_extender_1_out, multiplexer_2_out, ram_1_data;
  wire [19:7] rom_1_data_2;

  Decoder #(.select(3), .enable("false")) decoder_1 (
    .out0(decoder_1_out7[7]), .out1(decoder_1_out7[6]), .out2(decoder_1_out7[5]), .out3(decoder_1_out7[4]),
    .out4(decoder_1_out7[3]), .out5(decoder_1_out7[2]), .out6(decoder_1_out7[1]), .out7(decoder_1_out7[0]),
    .sel(rom_1_data_2[19:17]));
  Decoder #(.select(3), .enable("false")) decoder_2 (
    .out0(decoder_2_out6[7]), .out1(decoder_2_out6[6]), .out2(decoder_2_out6[5]), .out3(decoder_2_out6[4]),
    .out4(decoder_2_out6[3]), .out5(decoder_2_out6[2]), .out6(decoder_2_out6[1]), .out7(decoder_2_out6[0]),
    .sel(rom_1_data_2[16:14]));
  Decoder #(.select(3), .enable("false")) decoder_3 (
    .out0(decoder_3_out7[7]), .out1(decoder_3_out7[6]), .out2(decoder_3_out7[5]), .out3(decoder_3_out7[4]),
    .out4(decoder_3_out7[3]), .out5(decoder_3_out7[2]), .out6(decoder_3_out7[1]), .out7(decoder_3_out7[0]),
    .sel(rom_1_data_2[13:11]));
  not not_1 (not_1_out, decoder_1_out7[0]);
  Multiplexer #(.width(11), .enable("false")) multiplexer_1 (
    .in0(DR[10:0]), .in1(pc), .out(multiplexer_1_out), .sel(decoder_1_out7[1]));
  or or_1 (or_1_out, decoder_1_out7[2], decoder_1_out7[1]);
  AR_main u_PC (.d(AR), .LD(decoder_3_out7[1]), .inr(decoder_3_out7[2]), .clk(CLK), .clr(in_2), .Q(pc));
  or or_2 (or_2_out, decoder_3_out7[3], decoder_3_out7[4], decoder_1_out7[6], decoder_1_out7[4], decoder_2_out6[6]);
  Register #(.width(11)) register_1 (.D(multiplexer_1_out), .en(or_1_out), .Q(AR), .clk(CLK));  // open: clr
  not not_2 (not_2_out, main_1_p30);
  J_K_Flip_Flop j_k_ff_1 (
    .J(main_1_p30), .clk(CLK), .K(not_2_out), .Q(j_k_ff_1_q), .en(or_2_out));  // open: Qn, preset, reset
  or or_3 (or_3_out, decoder_2_out6[3], decoder_2_out6[0], decoder_2_out6[2]);
  assign bit_extender_1_out = {{5{1'b0}}, pc};  // Bit_Extender bit_extender_1
  Multiplexer #(.select(2), .width(16), .enable("false")) multiplexer_2 (
    .in0(ram_1_data), .in1(AC), .in2(bit_extender_1_out), .in3({16{1'b0}}), .out(multiplexer_2_out),
    .sel({decoder_2_out6[0], decoder_2_out6[2]}));
  // ac_main main_1: pin names not known; wires that end beside it: decoder_1_out7[6], decoder_1_out7[3], decoder_2_out6[6], decoder_2_out6[5], decoder_2_out6[4], decoder_3_out7[6], decoder_3_out7[5], decoder_3_out7[4], decoder_3_out7[3], DR, CLK, j_k_ff_1_q, decoder_1_out7[5], AC[0], AC[1], AC[2], AC[3], AC[4], AC[5], AC[6], AC[7], AC[8], AC[9], AC[10], AC[11], AC[12], AC[13], AC[14], AC[15], main_1_p30
  RAM #(.addrWidth(11), .dataWidth(16)) ram_1 (
    .addr(AR), .data(ram_1_data), .sel(1'b1), .clk(CLK), .ld(not_1_out));  // open: clr
  // _16_bit_register_with_inc_main dr: pin names not known; wires that end beside it: multiplexer_2_out, or_3_out, decoder_2_out6[1], CLK, DR
  or or_4 (or_4_out, AC[0], AC[1], AC[2], AC[3], AC[4], AC[5], AC[6], AC[7], AC[8], AC[9], AC[10], AC[11], AC[12], AC[13], AC[14], AC[15]);
  assign ram_1_data = decoder_1_out7[0] ? DR : 16'bz;  // Controlled_Buffer controlled_buffer_1
  car_inc_main main_2 (.d(CAR_q), .inr(1'b1), .clk(CLK), .Q(main_2_q));  // open: clr
  Register #(.width(7)) CAR (.D(mux_op), .en(1'b1), .Q(CAR_q), .clk(CLK));  // open: clr
  Register #(.width(7)) u_SBR (.D(main_2_q), .en(main_3_p1), .Q(sbr), .clk(CLK));  // open: clr
  Multiplexer #(.width(7), .enable("false")) multiplexer_3 (.in0(init_add), .in1(CAR_q), .out(ad_cm), .sel(S));
  Multiplexer #(.select(2), .width(7), .enable("false")) multiplexer_4 (
    .in0(main_2_q), .in1(rom_1_data), .in2(sbr), .in3({1'b0, DR[14:11], 2'b00}), .out(mux_op), .sel(s0s1));
  ROM #(.addrWidth(7), .dataWidth(20)) rom_1 (.addr(ad_cm), .data({rom_1_data_2, rom_1_data}), .sel(1'b1));
  // CU_SELECTER_CIRCUIT_main main_3: pin names not known; wires that end beside it: main_3_p1, s0s1[0], s0s1[1], main_3_p4, rom_1_data_2[7], rom_1_data_2[8]
  not not_3 (not_3_out, s0s1[1]);
  not not_4 (not_4_out, s0s1[0]);
  or or_5 (or_5_out, not_3_out, not_4_out);
  Multiplexer #(.select(2), .enable("false")) multiplexer_5 (
    .in0(1'b1), .in1(DR[15]), .in2(AC[15]), .in3(or_4_out), .out(main_3_p4), .sel(rom_1_data_2[10:9]));

  // Notes on the sheet:
  //   contents of rom_1 (hex, n*v repeats v):
  //   2c4 10002 20040 2840 418 40 2c4 3040 2c4 1400a e0040 0 2c4 1000e 9400f e0080 2c4 10012 80013 40 2c4
  //   10016 4040 0 2c4 304 37*0 c0000 c0041 12842 a0180 0 10045 a0180 0 0 45c a0100 26*0 c0000 12800 a0180
  //   0 10045 a0180
endmodule
