// Logisim project CU.circ as structural Verilog: 1 circuit, main circuit main
module main (
  input  [3:0] DR11_12_13_14,
  input  U,
  input  I,
  input  S,
  input  Z,
  input  CLK,
  output [2:0] F3,
  output [2:0] F2,
  output [2:0] F1
);

  wire INC_CAR_p4, main_1_p1, main_1_p4, not_1_out, not_2_out;
  wire [1:0] main_1_p2;
  wire [6:0] INC_CAR_p1, INC_CAR_p2, multiplexer_1_out, rom_1_data, SBR_q;
  wire [10:7] rom_1_data_2;

  // CAR_INCREMENTER_main INC_CAR: pin names not known; wires that end beside it: INC_CAR_p1, INC_CAR_p2, CLK, INC_CAR_p4
  Register #(.width(7)) CAR (.D(multiplexer_1_out), .en(1'b1), .Q(INC_CAR_p2), .clk(CLK));  // open: clr
  Register #(.width(7)) SBR (.D(INC_CAR_p1), .en(main_1_p1), .Q(SBR_q), .clk(CLK));  // open: clr
  ROM #(.addrWidth(7), .dataWidth(20)) rom_1 (
    .addr(INC_CAR_p2), .data({F1, F2, F3, rom_1_data_2, rom_1_data}), .sel(1'b1));
  Multiplexer #(.select(2), .width(7), .enable("false")) multiplexer_1 (
    .in0(INC_CAR_p1), .in1(rom_1_data), .in2(SBR_q), .in3({1'b0, DR11_12_13_14, 2'b00}),
    .out(multiplexer_1_out), .sel(main_1_p2));
  not not_1 (not_1_out, main_1_p2[1]);
  or or_1 (INC_CAR_p4, not_1_out, not_2_out);
  // CU_SELECTER_CIRCUIT_main main_1: pin names not known; wires that end beside it: main_1_p1, main_1_p2[0], main_1_p2[1], main_1_p4, rom_1_data_2[7], rom_1_data_2[8]
  not not_2 (not_2_out, main_1_p2[0]);
  Multiplexer #(.select(2), .enable("false")) multiplexer_2 (
    .in0(U), .in1(I), .in2(S), .in3(Z), .out(main_1_p4), .sel(rom_1_data_2[10:9]));

  // Notes on the sheet:
  //   contents of rom_1 (hex, n*v repeats v):
  //   2c4 10000 20040 97*0 c0000 12800 a0180
endmodule
