// Logisim project ac_test.circ as structural Verilog: 1 circuit, main circuit main
module main (
  input  [15:0] in_1,
  input  in_2,
  input  [9:0] in_3,
  input  in_4,
  output [15:0] out_5,
  output out_6
);

  // ac_main main_1: pin names not known; wires that end beside it: in_1, in_4, in_2, in_2, out_6
endmodule
