// Logisim project car_inc.circ as structural Verilog: 1 circuit, main circuit main
module main (
  input  [6:0] d,
  input  inr,
  input  clk,
  input  clr,
  output [6:0] Q
);

  wire main_1_p1, main_1_p4, main_2_p1, main_3_p1, main_4_p2, main_5_p2, main_6_p1, main_7_p4;
  wire [6:0] multiplexer_1_out;

  Multiplexer #(.width(7), .enable("false")) multiplexer_1 (.in1(d), .out(multiplexer_1_out), .sel(inr));  // open: in0
  // half_adder_main main_1: pin names not known; wires that end beside it: main_1_p1, Q[6], main_1_p1, main_1_p4, multiplexer_1_out[6], Q[5], main_1_p4
  // half_adder_main main_2: pin names not known; wires that end beside it: main_2_p1, multiplexer_1_out[5], main_2_p1
  // half_adder_main main_3: pin names not known; wires that end beside it: main_3_p1, multiplexer_1_out[3], Q[2], main_3_p1
  // half_adder_main main_4: pin names not known; wires that end beside it: Q[4], main_4_p2, multiplexer_1_out[4], Q[3], main_4_p2
  // half_adder_main main_5: pin names not known; wires that end beside it: Q[1], main_5_p2, multiplexer_1_out[1]
  // half_adder_main main_6: pin names not known; wires that end beside it: main_6_p1, multiplexer_1_out[2], main_6_p1
  // half_adder_main main_7: pin names not known; wires that end beside it: Q[0], main_5_p2, 1'b1, main_7_p4
  and and_1 (main_7_p4, inr, multiplexer_1_out[0]);
  Register #(.width(7)) register_1 (.D(multiplexer_1_out), .en(inr), .clk(clk), .clr(clr));  // open: Q
endmodule
